# Fritzing sketch System Architecture Wiring Diagram (saved by Fritzing 1.0.4)
breadboards: 1

parts:
  Raspberry_Pi_400 = Raspberry Pi 4B
  ADC1 = MCP3008 [package=dil16]
  DHT11 = TMP36 [package=to-92]
  PIR_Motion_Sensor = TMP36 [package=to-92]
  R1 = Photocell (LDR) [power=0.25W dark_resistance_@0.01lx=300kΩ light_resistance_@100lx=400Ω luminance=10lx package=THT]
  R2 = Resistor [tolerance=±5% resistance=220 package="0805 [SMD]"]
  R3 = Resistor [tolerance=±5% resistance=10k package="0805 [SMD]"]
  Piezo_Buzzer = Piezo Speaker
  LED1 = LED - 5mm [color="White (4500K)" current=0.030A package="5 mm [THT]"]

nets:
  3V3: Raspberry_Pi_400.3V3, Raspberry_Pi_400.GPIO4, ADC1.CH0, ADC1.VREF, ADC1.VDD, DHT11.VCC, DHT11.VOUT, R1.pin_0, R3.Pin_0, R3.Pin_1
  5V: Raspberry_Pi_400.5V, PIR_Motion_Sensor.VCC
  GND: Raspberry_Pi_400.GND, Raspberry_Pi_400.GPIO18, ADC1.DGND, ADC1.AGND, DHT11.GND, PIR_Motion_Sensor.GND, R1.pin_1, R2.Pin_0, Piezo_Buzzer.pin1, LED1.cathode
  N1: Raspberry_Pi_400.GPIO17, PIR_Motion_Sensor.VOUT
  N2: Raspberry_Pi_400.GPIO23, Piezo_Buzzer.pin2
  N3: Raspberry_Pi_400.GPIO10, ADC1.Din
  N4: Raspberry_Pi_400.GPIO9, ADC1.Dout
  N5: Raspberry_Pi_400.GPIO11, ADC1.CLK
  N6: Raspberry_Pi_400.GPIO8, ADC1.CS/SHDN
  N7: R2.Pin_1, LED1.anode
